# Fritzing sketch sketch (saved by Fritzing 0.9.3b)
circuit board: 8.46667cm x 5.64444cm

parts:
  U1 = NodeMCU V1.0
  Part1 = BME280 Breakout
  TFT1 = Color 320x240 TFT Display, ILI9341 Controller Chip

nets:
  N1: U1.D0, TFT1.Reset
  N2: U1.D1, Part1.SCK/SCL
  N3: U1.D2, Part1.SDI/SDA
  N4: U1.D4, TFT1.D/C
  3V3: U1.3V3, Part1.3.3V, TFT1.VCC, TFT1.LED
  GND: U1.GND, Part1.GND, TFT1.GND
  N5: U1.D5, TFT1.SCK
  N6: U1.D6, TFT1.SDO_(MISO)
  N7: U1.D7, TFT1.SDI_(MOSI)
  N8: U1.D8, TFT1.CS

custom parts:
  NodeMCU V1.0: ESP8266 based NodeMCU
  Color 320x240 TFT Display, ILI9341 Controller Chip: 2.2" TFT Display with ILI9341 Controller
